# Fritzing sketch Robot_v1 (saved by Fritzing 0.9.6b)
breadboards: 2

parts:
  Part1 = Arduino Uno (Rev3)
  Part2 = Arduino Nano (Rev3.0)
  Part5 = NRF24L01+ Breakout Board
  Part6 = Black Joystick KY-023
  Part7 = NRF24L01+ Breakout Board
  IR1 = TSOP312.., 314.. [package=THT]
  M1 = DC Motor
  M2 = DC Motor
  M3 = DC Motor
  M4 = DC Motor
  HC-SR04_Sensor_2 = HC-SR04 Ultrasonic Distance Sensor
  BAT1 = BC9VPC [package=bc9vpc]
  S1 = H-Bridge with L298N

nets (from the breadboard view):
  N1: Part1.D8, Part7.CS
  N2: Part1.D9_PWM, S1.IN3
  N3: Part1.D10_PWM/SS, S1.IN4
  N4: Part1.D11_PWM/MOSI, Part7.MOSI
  N5: Part1.D12/MISO, Part7.MISO
  N6: Part1.D13/SCK, Part7.SCK
  GND: Part1.GND, Part7.GND, IR1.GND, HC-SR04_Sensor_2.GND, BAT1.V+, S1.GND
  N7: Part1.D2, HC-SR04_Sensor_2.ECHO
  N8: Part1.D3_PWM, IR1.Data
  N9: Part1.D4, HC-SR04_Sensor_2.TRIG
  N10: Part1.D5_PWM, S1.IN1
  N11: Part1.D6_PWM, S1.IN2
  N12: Part1.D7, Part7.CE
  3V3: Part1.3V3, Part7.VCC
  5V: Part1.5V, IR1.Vs, HC-SR04_Sensor_2.VCC, S1.5V
  GND_2: Part2.GND, Part5.GND, Part6.GND
  N13: Part2.D7, Part5.CE
  N14: Part2.D8, Part5.CS
  N15: Part2.D11/MOSI, Part5.MOSI
  N16: Part2.D12/MISO, Part5.MISO
  5V_2: Part2.5V, Part6.+5V
  N17: Part2.A1, Part6.VRy
  N18: Part2.A0, Part6.VRx
  3V3_2: Part2.3V3, Part5.VCC
  N19: Part2.D13/SCK, Part5.SCK
  N20: M1.pin_1, M2.pin_1, S1.M1-02
  N21: M1.pin_2, M2.pin_2, S1.M1-01
  N22: M3.pin_1, M4.pin_1, S1.M2-02
  N23: M3.pin_2, M4.pin_2, S1.M2-01
  N24: BAT1.V-, S1.12V

notes:
  This ultasonc sensor will be placed on the front of the cart to enssure that collisions do not occur
  For comunication between the remote and the robot
  This will be the remote control for the robot if I revive an rf module on time

custom parts:
  Black Joystick KY-023: Description: The joystick is a combination of 2 analoog potentiometer and a digital switch. Arduino GND --> Module pin - Arduino +5V --> Module pin +5V Arduino Analoog 0 --> Module VRx Arduino Analoog 1 --> Module VRy Arduino Digital --> Module SW Dimensions: 1" x 1.25"
  HC-SR04 Ultrasonic Distance Sensor: The HC-SR04 is an ultrasonic distance sensor. It is capable of providing measurement for ranges of 2cm to 400cm. The module operates at 5V.
  H-Bridge with L298N: h-bridge
